// Logisim project 8.circ as structural Verilog: 2 circuits, main circuit main
module main (
);

  wire clock_1_out, my7472_1_q, my7472_2_q, my7472_3_q, my7472_4_q;

  Clock clock_1 (.out(clock_1_out));
  my7472 my7472_1 (
    .notS(1'b1), .K0(1'b1), .K1(1'b1), .K2(1'b1), .C(clock_1_out), .J0(1'b1), .J1(1'b1), .J2(1'b1),
    .notR(1'b1), .Q(my7472_1_q));  // open: notQ
  my7472 my7472_2 (
    .notS(1'b1), .K0(my7472_1_q), .K1(my7472_3_q), .K2(my7472_3_q), .C(clock_1_out), .J0(my7472_3_q),
    .J1(my7472_3_q), .J2(my7472_1_q), .notR(1'b1), .Q(my7472_2_q));  // open: notQ
  my7472 my7472_3 (
    .notS(1'b1), .K0(my7472_1_q), .K1(my7472_1_q), .K2(my7472_1_q), .C(clock_1_out), .J0(my7472_1_q),
    .J1(my7472_1_q), .J2(my7472_1_q), .notR(1'b1), .Q(my7472_3_q));  // open: notQ
  my7472 my7472_4 (
    .notS(1'b1), .K0(my7472_3_q), .K1(my7472_2_q), .K2(my7472_1_q), .C(clock_1_out), .J0(my7472_3_q),
    .J1(my7472_2_q), .J2(my7472_1_q), .notR(1'b1), .Q(my7472_4_q));  // open: notQ
  // Digital_Oscilloscope #(.nState(16)) digital_oscilloscope_1: pin names not known; wires that end beside it: clock_1_out, my7472_1_q, my7472_3_q, my7472_2_q, my7472_4_q
endmodule

module my7472 (
  input  notS,
  input  K0,
  input  K1,
  input  K2,
  input  C,
  input  J0,
  input  J1,
  input  J2,
  input  notR,
  output Q,
  output notQ
);

  wire and_1_out, and_2_out, not_1_out, not_2_out;

  not not_1 (not_1_out, notS);
  and and_1 (and_1_out, K0, K1, K2);
  and and_2 (and_2_out, J0, J1, J2);
  not not_2 (not_2_out, notR);
  J_K_Flip_Flop j_k_ff_1 (
    .J(and_2_out), .K(and_1_out), .clk(C), .Q(Q), .Qn(notQ), .preset(not_1_out), .reset(not_2_out));
endmodule
