// Logisim project 1.circ as structural Verilog: 1 circuit, main circuit main
module main (
  input  C1,
  input  [1:0] AB1,
  input  C,
  input  D,
  input  [1:0] AB,
  output out_6,
  output out_7
);

  wire and_1_out, and_2_out, not_1_out, not_2_out, not_3_out, or_1_out;

  not not_1 (not_1_out, C1);
  not not_2 (not_2_out, C);
  not not_3 (not_3_out, D);
  and and_1 (and_1_out, not_2_out, D);
  and and_2 (and_2_out, C, not_3_out);
  Multiplexer #(.select(2)) multiplexer_1 (
    .in0(1'b1), .in1(C1), .in2(not_1_out), .in3(not_1_out), .out(out_6), .sel(AB1));
  or or_1 (or_1_out, not_2_out, and_2_out);
  Multiplexer #(.select(2)) multiplexer_2 (
    .in0(and_1_out), .in1(or_1_out), .in2(and_1_out), .in3(and_1_out), .out(out_7), .sel(AB));
endmodule
