// Logisim project 2.circ as structural Verilog: 2 circuits, main circuit main
module main (
  input  [7:0] low127_0,
  input  [7:0] hight255_128,
  output out_3,
  output out_4,
  output out_5
);

  wire C_out, cnt_1_q3;
  wire [2:0] cnt_1_q0;

  Clock C (.out(C_out));
  cnt cnt_1 (.C(C_out), .Q0(cnt_1_q0[0]), .Q1(cnt_1_q0[1]), .Q2(cnt_1_q0[2]), .Q3(cnt_1_q3));
  Multiplexer #(.select(3)) multiplexer_1 (
    .in0(low127_0[0]), .in1(low127_0[1]), .in2(low127_0[2]), .in3(low127_0[3]), .in4(low127_0[4]),
    .in5(low127_0[5]), .in6(low127_0[6]), .in7(low127_0[7]), .out(out_3), .sel(cnt_1_q0));
  Multiplexer #(.select(3)) multiplexer_2 (
    .in0(hight255_128[0]), .in1(hight255_128[1]), .in2(hight255_128[2]), .in3(hight255_128[3]),
    .in4(hight255_128[4]), .in5(hight255_128[5]), .in6(hight255_128[6]), .in7(hight255_128[7]), .out(out_5),
    .sel(cnt_1_q0));
  Multiplexer multiplexer_3 (.in0(out_3), .in1(out_5), .out(out_4), .sel(cnt_1_q3));
endmodule

module cnt (
  input  C,
  output Q0,
  output Q1,
  output Q2,
  output Q3
);

  wire j_k_ff_1_q, j_k_ff_2_q, j_k_ff_3_q;

  J_K_Flip_Flop j_k_ff_1 (.J(1'b1), .K(1'b1), .clk(C), .Q(j_k_ff_1_q), .Qn(Q0));  // open: preset, reset
  J_K_Flip_Flop j_k_ff_2 (.J(1'b1), .K(1'b1), .clk(j_k_ff_1_q), .Q(j_k_ff_2_q), .Qn(Q1));  // open: preset, reset
  J_K_Flip_Flop j_k_ff_3 (.J(1'b1), .K(1'b1), .clk(j_k_ff_2_q), .Q(j_k_ff_3_q), .Qn(Q2));  // open: preset, reset
  J_K_Flip_Flop j_k_ff_4 (.J(1'b1), .K(1'b1), .clk(j_k_ff_3_q), .Qn(Q3));  // open: Q, preset, reset
endmodule
