// Logisim project 3.circ as structural Verilog: 2 circuits, main circuit main
module main (
  input  [3:0] A,
  input  [3:0] B,
  output [3:0] Q
);

  adder_4bit adder_4bit_1 (
    .Q0(Q[0]), .Q3(Q[3]), .Q1(Q[1]), .Q2(Q[2]), .A0(A[0]), .B0(B[0]), .A3(A[3]), .B3(B[3]), .A1(A[1]),
    .B1(B[1]), .A2(A[2]), .B2(B[2]));  // open: Cn, C_in
endmodule

module adder_4bit (
  input  A0,
  input  A2,
  input  A1,
  input  B0,
  input  B2,
  input  C_in,
  input  B1,
  input  A3,
  input  B3,
  output Q0,
  output Q2,
  output Q1,
  output Q3,
  output Cn
);

  wire not_1_out, not_2_out, not_3_out, not_4_out;
  wire [1:1] multiplexer_2_out, multiplexer_6_out, multiplexer_8_out;

  not not_1 (not_1_out, A0);
  Multiplexer #(.select(2)) multiplexer_1 (
    .in0(A0), .in1(not_1_out), .in2(not_1_out), .in3(A0), .out(Q0), .sel({C_in, B0}));
  Multiplexer #(.select(2)) multiplexer_2 (
    .in0(1'b0), .in1(A0), .in2(A0), .in3(1'b1), .out(multiplexer_2_out[1]), .sel({C_in, B0}));
  not not_2 (not_2_out, A1);
  not not_3 (not_3_out, A3);
  Multiplexer #(.select(2)) multiplexer_3 (
    .in0(A1), .in1(not_2_out), .in2(not_2_out), .in3(A1), .out(Q1), .sel({multiplexer_2_out[1], B1}));
  Multiplexer #(.select(2)) multiplexer_4 (
    .in0(A3), .in1(not_3_out), .in2(not_3_out), .in3(A3), .out(Q3), .sel({multiplexer_8_out[1], B3}));
  Multiplexer #(.select(2)) multiplexer_5 (
    .in0(1'b0), .in1(A3), .in2(A3), .in3(1'b1), .out(Cn), .sel({multiplexer_8_out[1], B3}));
  Multiplexer #(.select(2)) multiplexer_6 (
    .in0(1'b0), .in1(A1), .in2(A1), .in3(1'b1), .out(multiplexer_6_out[1]), .sel({multiplexer_2_out[1], B1}));
  not not_4 (not_4_out, A2);
  Multiplexer #(.select(2)) multiplexer_7 (
    .in0(A2), .in1(not_4_out), .in2(not_4_out), .in3(A2), .out(Q2), .sel({multiplexer_6_out[1], B2}));
  Multiplexer #(.select(2)) multiplexer_8 (
    .in0(1'b0), .in1(A2), .in2(A2), .in3(1'b1), .out(multiplexer_8_out[1]), .sel({multiplexer_6_out[1], B2}));
endmodule
