// Logisim project 5.circ as structural Verilog: 1 circuit, main circuit main
module main (
  input  in_1,
  input  in_2,
  input  in_3,
  input  in_4,
  input  in_5,
  input  in_6,
  input  in_7,
  output out_8,
  output out_9
);

  ROM #(.addrWidth(3), .dataWidth(1)) rom_1 (.addr({in_3, in_2, in_1}));  // open: data
  ROM #(.addrWidth(4), .dataWidth(1)) rom_2 (.addr({in_7, in_6, in_5, in_4}));  // open: data

  // Notes on the sheet:
  //   contents of rom_1 (hex, n*v repeats v):
  //   1 1 0 1 1 0 1
  //   contents of rom_2 (hex, n*v repeats v):
  //   1 0 0 1 1 1 0 0 1 0 0 0 1
endmodule
